// Digital circuit P01.dig as structural Verilog
module P01 (
  input  [7:0] a,
  input  [7:0] b,
  input  sub,
  output [7:0] y,
  output c,
  output v
);

  wire and_1_out, and_2_out, and_3_out, and_4_out, and_5_out, and_6_out, and_7_out, and_8_out, and_9_out,
       and_10_out, and_11_out, and_12_out, and_13_out, and_14_out, and_15_out, and_16_out, or_1_out,
       or_2_out, or_3_out, or_4_out, or_5_out, or_6_out, or_7_out, xor_1_out, xor_2_out, xor_3_out,
       xor_4_out, xor_5_out, xor_6_out, xor_7_out, xor_8_out, xor_9_out, xor_10_out, xor_11_out, xor_12_out,
       xor_13_out, xor_14_out, xor_15_out, xor_16_out;

  xor xor_1 (xor_1_out, b[0], sub);
  xor xor_2 (xor_2_out, b[1], sub);
  xor xor_3 (xor_3_out, b[2], sub);
  xor xor_4 (xor_4_out, b[3], sub);
  xor xor_5 (xor_5_out, b[4], sub);
  xor xor_6 (xor_6_out, b[5], sub);
  xor xor_7 (xor_7_out, b[6], sub);
  xor xor_8 (xor_8_out, b[7], sub);
  xor xor_9 (xor_9_out, xor_1_out, a[0]);
  xor xor_10 (xor_10_out, xor_2_out, a[1]);
  xor xor_11 (xor_11_out, xor_3_out, a[2]);
  xor xor_12 (xor_12_out, xor_4_out, a[3]);
  xor xor_13 (xor_13_out, xor_5_out, a[4]);
  xor xor_14 (xor_14_out, xor_6_out, a[5]);
  xor xor_15 (xor_15_out, xor_7_out, a[6]);
  xor xor_16 (xor_16_out, xor_8_out, a[7]);
  and and_1 (and_1_out, a[0], xor_1_out);
  and and_2 (and_2_out, a[1], xor_2_out);
  and and_3 (and_3_out, a[2], xor_3_out);
  and and_4 (and_4_out, a[3], xor_4_out);
  and and_5 (and_5_out, a[4], xor_5_out);
  and and_6 (and_6_out, a[5], xor_6_out);
  and and_7 (and_7_out, a[6], xor_7_out);
  and and_8 (and_8_out, a[7], xor_8_out);
  xor xor_17 (y[0], sub, xor_9_out);
  xor xor_18 (y[1], or_1_out, xor_10_out);
  xor xor_19 (y[2], or_2_out, xor_11_out);
  xor xor_20 (y[3], or_3_out, xor_12_out);
  xor xor_21 (y[4], or_4_out, xor_13_out);
  xor xor_22 (y[5], or_5_out, xor_14_out);
  xor xor_23 (y[6], or_6_out, xor_15_out);
  xor xor_24 (y[7], or_7_out, xor_16_out);
  and and_9 (and_9_out, sub, xor_9_out);
  and and_10 (and_10_out, xor_10_out, or_1_out);
  and and_11 (and_11_out, xor_11_out, or_2_out);
  and and_12 (and_12_out, xor_12_out, or_3_out);
  and and_13 (and_13_out, xor_13_out, or_4_out);
  and and_14 (and_14_out, xor_14_out, or_5_out);
  and and_15 (and_15_out, xor_15_out, or_6_out);
  and and_16 (and_16_out, xor_16_out, or_7_out);
  or or_1 (or_1_out, and_1_out, and_9_out);
  or or_2 (or_2_out, and_2_out, and_10_out);
  or or_3 (or_3_out, and_3_out, and_11_out);
  or or_4 (or_4_out, and_4_out, and_12_out);
  or or_5 (or_5_out, and_5_out, and_13_out);
  or or_6 (or_6_out, and_6_out, and_14_out);
  or or_7 (or_7_out, and_7_out, and_15_out);
  or or_8 (c, and_8_out, and_16_out);
  xor xor_25 (v, or_7_out, c);

  // Notes on the sheet:
  //   P01 ALU adder/subtractor - Digital task
  //   8-bit version. Build a full adder from gates first, then chain eight of them; XOR gates on b make the subtractor.
  //   Allowed parts: And, Or, Not, NAnd, NOr, XOr, XNOr + wiring parts
  //   Do not rename, move or delete the input and output pins.
endmodule

/* Test case public tests:
a b sub y c v
245 2 1 243 1 0
255 182 1 73 1 0
252 255 0 251 1 0
222 7 1 215 1 0
0 128 0 128 0 0
3 37 0 40 0 0
127 127 0 254 0 1
76 28 0 104 0 0
144 13 1 131 1 0
11 11 1 0 1 0
127 128 0 255 0 0
14 124 0 138 0 1
232 0 0 232 0 0
255 67 0 66 1 0
0 128 1 128 0 1
23 132 0 155 0 0
128 80 0 208 0 0
0 177 1 79 0 0
128 6 1 122 1 1
30 17 1 13 1 0
12 252 0 8 1 0
61 243 1 74 0 0
128 100 1 28 1 1
130 6 1 124 1 1
122 54 1 68 1 0
0 0 1 0 1 0
185 255 1 186 0 0
0 255 1 1 0 0
89 0 0 89 0 0
3 22 0 25 0 0
8 152 0 160 0 0
24 0 1 24 1 0
27 214 0 241 0 0
128 203 1 181 0 0
1 197 1 60 0 0
9 1 0 10 0 0
193 128 1 65 1 0
16 12 1 4 1 0
63 76 0 139 0 1
0 255 0 255 0 0
9 82 0 91 0 0
14 127 0 141 0 1
61 220 0 25 1 0
4 15 0 19 0 0
128 233 0 105 1 1
55 0 0 55 0 0
205 175 0 124 1 1
16 151 0 167 0 0
188 24 1 164 1 0
255 243 1 12 1 0
1 128 0 129 0 0
106 180 0 30 1 0
127 20 1 107 1 0
202 218 0 164 1 0
123 8 0 131 0 1
128 92 1 36 1 1
18 144 1 130 0 1
0 12 0 12 0 0
215 180 0 139 1 0
186 172 1 14 1 0
128 100 1 28 1 1
14 14 0 28 0 0
68 34 1 34 1 0
13 226 1 43 0 0
16 99 0 115 0 0
24 164 1 116 0 0
249 12 1 237 1 0
255 131 1 124 1 0
176 188 0 108 1 1
128 127 1 1 1 1
39 169 0 208 0 0
188 255 1 189 0 0
0 12 1 244 0 0
128 254 1 130 0 0
3 1 1 2 1 0
153 128 0 25 1 1
17 152 1 121 0 0
142 127 1 15 1 1
84 16 1 68 1 0
0 28 1 228 0 0
171 22 1 149 1 0
26 16 0 42 0 0
68 76 1 248 0 0
255 128 0 127 1 1
0 60 0 60 0 0
255 182 1 73 1 0
101 110 1 247 0 0
15 0 0 15 0 0
186 1 0 187 0 0
11 21 0 32 0 0
231 15 0 246 0 0
228 186 1 42 1 0
193 254 0 191 1 0
72 11 1 61 1 0
33 7 0 40 0 0
0 19 1 237 0 0
52 236 0 32 1 0
0 183 0 183 0 0
30 255 1 31 0 0
22 128 1 150 0 1
127 127 1 0 1 0
22 26 0 48 0 0
24 29 1 251 0 0
2 77 0 79 0 0
60 128 0 188 0 0
127 236 1 147 0 1
78 99 1 235 0 0
59 110 0 169 0 1
117 255 0 116 1 0
241 128 1 113 1 0
26 128 0 154 0 0
105 104 1 1 1 0
229 24 0 253 0 0
255 235 0 234 1 0
22 106 0 128 0 1
27 128 0 155 0 0
127 200 0 71 1 0
200 58 1 142 1 0
237 216 0 197 1 0
228 104 0 76 1 0
24 0 0 24 0 0
153 50 0 203 0 0
162 127 1 35 1 1
255 168 0 167 1 0
205 19 0 224 0 0
12 255 1 13 0 0
231 14 1 217 1 0
16 28 1 244 0 0
141 4 1 137 1 0
25 0 0 25 0 0
255 14 0 13 1 0
94 0 1 94 1 0
213 27 1 186 1 0
247 128 0 119 1 1
0 128 1 128 0 1
22 4 1 18 1 0
167 0 1 167 1 0
7 6 0 13 0 0
62 84 1 234 0 0
0 123 1 133 0 0
4 106 0 110 0 0
24 14 1 10 1 0
129 126 0 255 0 0
0 184 1 72 0 0
255 0 1 255 1 0
37 17 0 54 0 0
141 0 0 141 0 0
128 255 0 127 1 1
57 0 1 57 1 0
0 240 1 16 0 0
12 128 0 140 0 0
26 217 1 65 0 0
128 240 1 144 0 0
226 22 0 248 0 0
111 44 0 155 0 1
33 2 0 35 0 0
74 28 1 46 1 0
7 41 1 222 0 0
255 96 0 95 1 0
151 255 0 150 1 0
*/
